// Digital circuit Praktikum 5 Digital.dig as structural Verilog
module Praktikum_5_Digital (
  input  A,
  input  B,
  input  C,
  output X
);

  wire and_1_out, and_2_out, not_1_out, not_2_out, or_1_out;

  not not_1 (not_1_out, C);
  not not_2 (not_2_out, B);
  or or_1 (or_1_out, A, not_1_out);
  and and_1 (and_1_out, not_2_out, C);
  and and_2 (and_2_out, and_1_out, or_1_out);
  or or_2 (X, A, B, and_2_out);
endmodule
