// Digital circuit Praktikum 6 Digital.dig as structural Verilog
module Praktikum_6_Digital (
  input  A,
  input  B,
  output X
);

  wire not_1_out, not_2_out, or_1_out, or_2_out, or_3_out;

  not not_1 (not_1_out, A);
  or or_1 (or_1_out, A, B);
  not not_2 (not_2_out, B);
  or or_2 (or_2_out, A, not_2_out);
  or or_3 (or_3_out, not_1_out, B);
  and and_1 (X, or_1_out, or_2_out, or_3_out);
endmodule
