// Digital circuit RANGKAIAN-DIGITAL.dig as structural Verilog
module RANGKAIAN_DIGITAL (
  input  A1,
  input  A2,
  input  A3,
  input  A4,
  input  A5,
  input  A7,
  input  A8,
  input  A9,
  output X,
  output Y,
  output Z,
  output XY,
  output Z_2,
  output XY_2
);

  or or_1 (X, A1, 1'b1);
  or or_2 (Z, A3, A4);
  // Not not_1 is placed but not wired
  or or_3 (Z_2, A7, A8);
  // Not not_2 is placed but not wired
  and and_1 (Y, A2, 1'b1);
  and and_2 (XY, A5, A5);
  and and_3 (XY_2, A9, ~A9);  // And

  // Notes on the sheet:
  //   A + 1 = 1
  //   A + A = A
  //   A . 1 = 1
  //   A . A = A
endmodule
