// Digital circuit UTS_1_1.dig as structural Verilog
module UTS_1_1 (
  input  A,
  input  B,
  input  C
);

  wire and_1_out, or_1_out, or_2_out, or_3_out;

  or or_1 (or_1_out, A, A, A);
  and and_1 (and_1_out, A, A, A);
  or or_2 (or_2_out, A, A, A);
  or or_3 (or_3_out, or_1_out, or_2_out, and_1_out);
  LED X (.in(or_3_out));

  assign B = A;
  assign C = A;

  // Notes on the sheet:
  //   Rizki Nugraha
  //   1.(AB+AC+BC)'(A+B+C)+ABC
endmodule
