// Digital circuit UTS_1_11.dig as structural Verilog
module UTS_1_11 (
  input  x,
  input  y,
  input  z
);

  wire and_1_out, and_2_out, and_3_out, and_4_out, or_1_out;

  and and_1 (and_1_out, ~x, ~y, z);  // And
  and and_2 (and_2_out, x, y, ~z);  // And
  and and_3 (and_3_out, ~x, y, z);  // And
  and and_4 (and_4_out, x, y);
  or or_1 (or_1_out, and_1_out, and_2_out, and_3_out, and_4_out);
  LED A (.in(or_1_out));

  // Notes on the sheet:
  //   Rizki Nugraha
  //   11. x'y'z + y'z' + x'yz+xy
endmodule
