// Digital circuit UTS_1_12.dig as structural Verilog
module UTS_1_12 (
  input  x,
  input  y,
  input  z
);

  wire and_1_out, and_2_out, and_3_out, not_1_out, or_1_out;

  not not_1 (not_1_out, z);
  and and_1 (and_1_out, x, z);
  and and_2 (and_2_out, x, y, not_1_out);
  and and_3 (and_3_out, ~y, ~x);  // And
  or or_1 (or_1_out, and_1_out, and_2_out, and_3_out);
  LED A (.in(or_1_out));

  // Notes on the sheet:
  //   Rizki Nugraha
  //   12. xyz' + y'z' + xz
endmodule
