// Digital circuit UTS_1_13.dig as structural Verilog
module UTS_1_13 (
  input  x,
  input  y,
  input  z
);

  wire and_1_out, and_2_out, and_3_out, or_1_out;

  and and_1 (and_1_out, x, ~y);  // And
  and and_2 (and_2_out, ~x, y, z);  // And
  and and_3 (and_3_out, y, ~z);  // And
  or or_1 (or_1_out, and_1_out, and_2_out, and_3_out);
  LED A (.in(or_1_out));

  // Notes on the sheet:
  //   Rizki Nugraha
  //   13. x'yz + xy' + yz'
endmodule
