// Digital circuit UTS_1_15.dig as structural Verilog
module UTS_1_15 (
  input  A,
  input  B,
  input  C,
  input  D
);

  wire and_1_out, and_2_out, and_3_out, and_4_out, or_1_out;

  and and_1 (and_1_out, A, B, ~C);  // And
  and and_2 (and_2_out, ~C, D);  // And
  and and_3 (and_3_out, ~A, C, ~D);  // And
  and and_4 (and_4_out, ~B, C, ~D);  // And
  or or_1 (or_1_out, and_1_out, and_2_out, and_3_out, and_4_out);
  LED X (.in(or_1_out));

  // Notes on the sheet:
  //   Rizki Nugraha
  //   15.ABC'+C'D+A'CD'+B'CD'
endmodule
