// Digital circuit UTS_1_2.dig as structural Verilog
module UTS_1_2 (
  input  D,
  input  B,
  input  A,
  input  C
);

  wire and_1_out, and_2_out, and_3_out, and_4_out, and_5_out, and_6_out, not_1_out, not_2_out, not_3_out,
       not_4_out, or_1_out;

  not not_1 (not_1_out, B);
  not not_2 (not_2_out, B);
  not not_3 (not_3_out, B);
  not not_4 (not_4_out, A);
  and and_1 (and_1_out, not_2_out, not_3_out, not_4_out);
  and and_2 (and_2_out, not_4_out, B);
  and and_3 (and_3_out, not_4_out, not_2_out, not_1_out);
  and and_4 (and_4_out, not_4_out, B);
  and and_5 (and_5_out, A, B, B);
  and and_6 (and_6_out, not_4_out, not_3_out);
  or or_1 (or_1_out, and_1_out, and_5_out, and_2_out, and_6_out, and_3_out, and_4_out);
  LED led_1 (.in(or_1_out));

  assign C = B;
  assign D = B;

  // Notes on the sheet:
  //   Rizki Nugraha
  //   2.A'B'C'+A'CD+A'C'D'+A'BD+ABC+AB'C
endmodule
