// Digital circuit UTS_1_7.dig as structural Verilog
module UTS_1_7 (
  input  W,
  input  X,
  input  Y,
  input  Z
);

  wire and_1_out, and_2_out, and_3_out, and_4_out, or_1_out;

  and and_1 (and_1_out, ~W, ~X, Z);  // And
  and and_2 (and_2_out, X, ~Y);  // And
  and and_3 (and_3_out, ~W, X);  // And
  and and_4 (and_4_out, W, X, Y);
  or or_1 (or_1_out, and_1_out, and_2_out, and_3_out, and_4_out);
  LED A (.in(or_1_out));

  // Notes on the sheet:
  //   Rizki Nugraha
  //   7.w'x'z+xy'+w'x+wxy
endmodule
