// Digital circuit UTS_1_8.dig as structural Verilog
module UTS_1_8 (
  input  A,
  input  B,
  input  C,
  input  D
);

  wire and_1_out, and_2_out, and_3_out, and_4_out, and_5_out, or_1_out;

  and and_1 (and_1_out, ~A, A, ~A);  // And
  and and_2 (and_2_out, A, A, C);
  and and_3 (and_3_out, A, A);
  and and_4 (and_4_out, A, A, C);
  and and_5 (and_5_out, A, A, ~C);  // And
  or or_1 (or_1_out, and_1_out, and_2_out, and_5_out, and_3_out, and_4_out);
  LED X (.in(or_1_out));

  assign B = A;
  assign D = A;

  // Notes on the sheet:
  //   Rizki Nugraha
  //   8.A'BD'+BDC+ABC'+BD+ABC
endmodule
